# Fritzing sketch Rancangan tugas akhir (saved by Fritzing 0.9.3b)
breadboards: 1

parts:
  Part1 = Arduino Uno (Rev3)
  LED1 = RGB LED (com. cathode, rbg) [package="5 mm [THT]"]
  LED2 = smd LED [color="Red (633nm)" package="0603 [SMD]"]
  S1 = Pushbutton [package="[SMD]"]
  hc-sr1 = hc-sr04
  Part2 = LCD1602-I2C
  R1 = Resistor [tolerance=±5% resistance=220 package=THT]
  J1 = Piezo Speaker

nets:
  N1: Part1.A4/SDA, Part2.SDA
  N2: Part1.A5/SCL, Part2.SCL
  N3: Part1.D8, LED2.cathode
  N4: Part1.D9_PWM, S1.Pin_1, S1.Pin_2
  N5: Part1.D10_PWM/SS, J1.pin1
  N6: Part1.D11_PWM/MOSI, LED1.red_anode
  N7: Part1.D12/MISO, LED1.common_cathode
  N8: Part1.D13/SCK, LED1.green_anode
  N9: Part1.D2, hc-sr1.Echo
  N10: Part1.D4, hc-sr1.Trig
  VCC: Part1.5V, LED2.anode, hc-sr1.VCC, Part2.VCC, R1.Pin_1, J1.pin2
  GND: Part1.GND, S1.Pin_3, S1.Pin_4, hc-sr1.GND, Part2.GND
  N11: LED1.blue_anode, R1.Pin_0

custom parts:
  LCD1602-I2C: A standard character display, usually with 2x16 characters. Comes in many colors with LCM1602 IIC attached.
